# Fritzing sketch drawer_sketch (saved by Fritzing 0.7.12b)
breadboards: 1

parts:
  Arduino1 = Arduino
  J1 = Basic Servo
  J2 = Infrared Proximity Sensor
  IC1 = IC, DIP package, 16 pins [chip_label=IC]
  M1 = DC Motor
  M2 = DC Motor
  R3 = Resistor [tolerance=±5% resistance=10k package=THT]
  R4 = Resistor [tolerance=±5% resistance=10k package=THT]
  R5 = Photocell (LDR) [package=THT]
  R6 = Photocell (LDR) [package=THT]
  Part1 = Bluetooth Mate Silver
  LED1 = LED - 5mm [color="Red (633nm)" package="5 mm [THT]"]
  C1 = Ceramic Capacitor [capacitance=100nF package="100 mil [THT, multilayer]"]

nets:
  GND: Arduino1.GND, J1.gnd, J2.GND, R3.Pin_0, R4.Pin_0, Part1.GND, LED1.cathode, C1.1
  N1: Arduino1.D13, LED1.anode
  N2: Arduino1.D10, IC1.pin1
  N3: Arduino1.D9, IC1.pin2
  N4: Arduino1.D8, IC1.pin7
  N5: Arduino1.D5, IC1.pin15
  N6: Arduino1.D4, IC1.pin10
  N7: Arduino1.D3, IC1.pin9
  VCC: Arduino1.D2, Arduino1.VIN, J1.vcc, J2.Vcc, IC1.pin8, IC1.pin16, R5.pin_1, R6.pin_1, Part1.VCC, C1.0
  N8: Arduino1.D1TX, Part1.RX_5V
  N9: Arduino1.D0RX, Part1.TX_5V
  N10: Arduino1.A4, R3.Pin_1, R5.pin_0
  N11: Arduino1.A5, R4.Pin_1, R6.pin_0
  N12: IC1.pin3, M2.pin_2
  N13: IC1.pin4, IC1.pin5, IC1.pin12, IC1.pin13
  N14: IC1.pin6, M2.pin_1
  N15: IC1.pin11, M1.pin_2
  N16: IC1.pin14, M1.pin_1
