# Fritzing sketch remote_sketch (saved by Fritzing 0.7.12b)
breadboards: 1

parts:
  R1 = Resistor [tolerance=±5% resistance=1k package=THT]
  S1 = Toggle Switch [package=THT]
  Arduino1 = Arduino
  R2 = Resistor [tolerance=±5% resistance=1k package=THT]
  S2 = Toggle Switch [package=THT]
  R3 = Resistor [tolerance=±5% resistance=1k package=THT]
  S3 = Toggle Switch [package=THT]
  S4 = Round Pushbutton
  S5 = Round Pushbutton
  S6 = Round Pushbutton
  S7 = Round Pushbutton
  R4 = Resistor [tolerance=±5% resistance=2.2k package=THT]
  R5 = Resistor [tolerance=±5% resistance=2.2k package=THT]
  R6 = Resistor [tolerance=±5% resistance=2.2k package=THT]
  R7 = Resistor [tolerance=±5% resistance=2.2k package=THT]
  Part1 = Bluetooth Mate Silver
  VCC1 = Battery block 9V

nets:
  N1: R1.Pin_0, S1.L1, Arduino1.D10
  VIN: R1.Pin_1, Arduino1.VIN, R2.Pin_1, R3.Pin_1, R4.Pin_1, R5.Pin_1, R6.Pin_1, R7.Pin_1, Part1.VCC, VCC1.+
  GND: S1.COM, Arduino1.GND, S2.COM, S3.COM, S4.leg1, S5.leg1, S6.leg1, S7.leg1, Part1.GND, VCC1.-
  N2: Arduino1.D9, R2.Pin_0, S2.L1
  N3: Arduino1.D8, R3.Pin_0, S3.L1
  N4: Arduino1.D5, S7.leg0, R7.Pin_0
  N5: Arduino1.D4, S6.leg0, R6.Pin_0
  N6: Arduino1.D3, S5.leg0, R5.Pin_0
  N7: Arduino1.D2, S4.leg0, R4.Pin_0
  N8: Arduino1.D1TX, Part1.TX_5V
  N9: Arduino1.D0RX, Part1.RX_5V

notes:
  I have NO and COM on the pushbuttons, NO goes to GND
  Battery heats up and goes wonky
